# Fritzing sketch VoltAndOhmmeter (saved by Fritzing 0.9.4)
breadboards: 1

parts:
  1602_LCD = LCD screen
  Arduino_Nano = Arduino Nano (Rev3.0)
  R12 = Trimmer Potentiometer [maximum_resistance=10kΩ package=THT]
  1% = Resistor [tolerance=±1% resistance=100k package=THT]
  1%_2 = Resistor [tolerance=±1% resistance=100k package=THT]
  1%_3 = Resistor [tolerance=±1% resistance=22k package=THT]
  1%_4 = Resistor [tolerance=±1% resistance=10k package=THT]
  R-unknown = Resistor [tolerance=±5% resistance=220k package=THT]

nets:
  VSS: 1602_LCD.VSS, 1602_LCD.R/W, 1602_LCD.LED-, Arduino_Nano.GND, R12.leg2, R-unknown.Pin_0
  5V: 1602_LCD.VDD, 1602_LCD.LED+, Arduino_Nano.5V, R12.leg1
  N1: 1602_LCD.V0, R12.wiper
  N2: 1602_LCD.RS, Arduino_Nano.D7
  N3: 1602_LCD.E, Arduino_Nano.D8
  N4: 1602_LCD.DB4, Arduino_Nano.D3
  N5: 1602_LCD.DB5, Arduino_Nano.D4
  N6: 1602_LCD.DB6, Arduino_Nano.D5
  N7: 1602_LCD.DB7, Arduino_Nano.D6
  N8: Arduino_Nano.A3, 1%_4.Pin_0
  N9: Arduino_Nano.A2, 1%_3.Pin_1
  N10: Arduino_Nano.A1, 1%.Pin_0
  N11: Arduino_Nano.A0, 1%_2.Pin_0, 1%_3.Pin_0
  N12: 1%.Pin_1, 1%_2.Pin_1, 1%_4.Pin_1, R-unknown.Pin_1

notes:
  Voltage or unknown resistor to ground
